# Fritzing sketch StudentSenseHatV03 (saved by Fritzing 0.9.3b)
circuit board: 5.5cm x 5.7cm
breadboards: 1

parts:
  LED1 = LED - 3mm [color="Red (633nm)" package="3 mm [THT]"]
  R1 = Resistor [tolerance=±5% resistance=1k package=THT]
  R2 = Resistor [tolerance=±5% resistance=3.9k package=THT]
  R3 = Resistor [tolerance=±5% resistance=3.9k package=THT]
  R5 = Resistor [tolerance=±5% resistance=4.7k package=THT]
  JP2 = Header 4 [part_number=DS3231 package=molex-1x4_lock]
  JP3 = Header 4 [part_number=PCF8591 package=molex-1x4_lock]
  JP4 = Header 4 [part_number=Expand package=molex-1x4_lock]
  Q4 = MOSFET-NCHANNEL [package=to-92]
  R4 = Resistor [tolerance=±5% resistance=4.7k package=THT]
  Q3 = MOSFET-NCHANNEL [package=to-92]
  Raspberry_Pi_1 = Raspberry Pi 3 [part_number=RPI-3-V1.2]

nets:
  N1: LED1.cathode, Raspberry_Pi_1.GPIO17
  N2: LED1.anode, R1.Pin_0
  N3: R1.Pin_1, Raspberry_Pi_1.GPIO8
  3V3: R2.Pin_0, R3.Pin_0, JP2.2, Q4.G, Q3.G, Raspberry_Pi_1.3v3, Raspberry_Pi_1.3V3
  3.3V SCL: R2.Pin_1, JP2.4, Q3.S, Raspberry_Pi_1.GPIO3
  3.3V SDA: R3.Pin_1, JP2.3, Q4.S, Raspberry_Pi_1.GPIO2
  N4: R5.Pin_0, JP3.1, JP4.2, R4.Pin_0, Raspberry_Pi_1.5V
  5V SCL: R5.Pin_1, JP3.4, JP4.4, Q3.D
  N5: JP2.1, JP3.2, JP4.1, Raspberry_Pi_1.GND
  5V SDA: JP3.3, JP4.3, Q4.D, R4.Pin_1

notes:
  5V
  PCF
  RTC
  GND
  SDA
  SCL
  3.3V
  DS3231
  PCF8591

custom parts:
  MOSFET-NCHANNEL: Generic NMOS footprint
